# Fritzing sketch GDSwithWemos (saved by Fritzing 0.9.9b)
breadboards: 1

parts:
  WeMos_D1_Mini1 = WeMos D1 Mini
  M1 = NEO-6M GPS Module [part_number=GY-GPS6MV2]

nets:
  5V: WeMos_D1_Mini1.5V, M1.Vcc
  N1: WeMos_D1_Mini1.D2, WeMos_D1_Mini1.G, M1.GND, M1.Rx
  N2: WeMos_D1_Mini1.D3, M1.Tx

custom parts:
  NEO-6M GPS Module: GY-GPS6MV2 NEO-6M GPS Module Module based on U-blox NEO-6M GPS engine, incorporating regulator for 3.3-5V DC input, MS621FE-compatible rechargeable battery for backup and EEPROM for storing configuration settings. Links: NEO-6 series product information page NEO-6 Datasheet
